# Fritzing sketch Buiten-binnen tank2 (saved by Fritzing 0.9.6b)
circuit board: 6cm x 9cm
breadboards: 1

parts:
  ERROR = screw terminal, 3 pins
  R5 = Resistor [tolerance=±5% power=0.25 resistance=220 package=THT]
  R4 = Resistor [tolerance=±5% power=0.25 resistance=220 package=THT]
  555 = 555 Timer [package="DIP8 [THT]"]
  Buiten = screw terminal, 3 pins
  Laag = screw terminal, 3 pins
  Half = screw terminal, 3 pins
  Vol = screw terminal, 3 pins
  Arduino_nano = Arduino Nano (Rev3.0)
  C1 = Electrolytic Capacitor [capacitance=1µF voltage=35V package="100 mil [THT, electrolytic]"]
  Pomp = Screw terminal - 2 pins [package=THT]
  LED5 = LED - 3mm [color="Red (633nm)" current=0.030 package="3 mm [THT]"]
  LED3 = LED - 3mm [color="Green (555nm)" current=0.030 package="3 mm [THT]"]
  R7 = Resistor [tolerance=±5% power=0.25 resistance=100k package=THT]
  LED6 = LED - 3mm [color="Blue (430nm)" current=0.030 package="3 mm [THT]"]
  LED1 = LED - 3mm [color="Red (633nm)" current=0.030 package="3 mm [THT]"]
  LED2 = LED - 3mm [color="Red (633nm)" current=0.030 package="3 mm [THT]"]
  R8 = Resistor [tolerance=±5% power=0.25 resistance=220 package=THT]
  R3 = Resistor [tolerance=±5% power=0.25 resistance=220 package=THT]
  R1 = Resistor [tolerance=±5% power=0.25 resistance=220 package=THT]
  LED4 = LED - 3mm [color="Green (555nm)" current=0.030 package="3 mm [THT]"]
  R6 = Resistor [tolerance=±5% power=0.25W resistance=1k package=THT]
  R2 = Resistor [tolerance=±5% power=0.25 resistance=220 package=THT]
  U2 = Optocoupler [package=THT]
  R9 = Resistor [tolerance=±5% power=0.25 resistance=220 package=THT]
  Error_out = screw terminal, 3 pins

nets:
  N1: ERROR.pin1, Buiten.pin1, Laag.pin1, Half.pin1, Vol.pin1, Arduino_nano.5V, R6.Pin_1
  N2: ERROR.pin2, R5.Pin_0, R4.Pin_0, 555.Ground, Buiten.pin2, Laag.pin2, Half.pin2, Vol.pin2, Arduino_nano.GND, C1.-, LED5.cathode, R3.Pin_0, R1.Pin_0, R2.Pin_0, U2.Pin_2, Error_out.pin1
  N3: ERROR.pin3, Arduino_nano.A0
  N4: R5.Pin_1, LED6.cathode
  N5: R4.Pin_1, LED4.cathode
  N6: 555.Trigger, 555.Threshold, C1.+, R7.Pin_0
  N7: 555.Output, R8.Pin_0
  N8: 555.Reset, 555.Vcc_Supply_Voltage, Arduino_nano.D6, Error_out.pin2
  N9: 555.Discharge, R7.Pin_1, R6.Pin_0
  N10: Buiten.pin3, Arduino_nano.A1
  N11: Laag.pin3, Arduino_nano.A2
  N12: Half.pin3, Arduino_nano.A3
  N13: Vol.pin3, Arduino_nano.A4
  N14: Arduino_nano.D2, LED1.anode
  N15: Arduino_nano.D3, LED2.anode, Error_out.pin3
  N16: Arduino_nano.D4, LED3.anode
  N17: Arduino_nano.D5, LED4.anode
  N18: Arduino_nano.D7, LED6.anode, R9.Pin_1
  N19: Pomp.pin1, U2.Pin_5
  N20: Pomp.pin2, U2.Pin_4
  N21: LED5.anode, R8.Pin_1
  N22: LED3.cathode, R3.Pin_1
  N23: LED1.cathode, R1.Pin_1
  N24: LED2.cathode, R2.Pin_1
  N25: U2.Pin_1, R9.Pin_0

notes:
  C17, elco 10µF
  R1- R5,R8 - R9 220
  R6 1k R7 100k
  Sig = geel
  5V = bruin
  Gnd = blauw

// code stored in the sketch: Onderzoeken.ino
/*Deze schets is zoniet de belagrijkste van de 3 schetsen waaruit de bewaking van de serre bestaat, 
 alhoewel er geen enkele van de serie gemist kan worden. Deze NANO zorgd er namelijk voor dat er 
voldoende water beschikbaar is. Er komt nog een uitbrijding van deze dewelke is dat als de buitentank 
leeg zou zijn die bijgevuld wordt uit een externe bron: stadwater bijvoorbeeld of indien aanwezig 
grondwater(boorput).
bij een ERROR geeft hij een signaal aan de andere  NANO die op zijn beurt het watergeven stopt als 
de binnentank leeg is om drooglopen te voorkomen. Sensor tank leeg van hier wordt doorgeschakelt 
om het leeg zijn vast te stellen. Maw, zowel ERROR en tank leeg HIGH stop het water gedeelte.
*/
#define sensor1  A1   //tank buiten
#define sensor2  A2   //tank binnen laag
#define sensor3  A3   //tank binnen midden
#define sensor4  A4   //tank binnen vol
#define sensor5  A0   //overloop allarm

#define led1    2   //buiten leeg
#define led2    3   //binnen leeg
#define led3    4   //binnen halfvol
#define led4    5   //binnen vol
#define led5    6   //error
#define led6    7    //pomp


int Sensor1 = 0;
int Sensor2 = 0;
int Sensor3 = 0;
int Sensor4 = 0;
int Sensor5 = 0;

void setup() {

  pinMode (sensor1, INPUT_PULLUP);//buiten tank
  pinMode (sensor2, INPUT_PULLUP);//binnen leeg
  pinMode (Sensor3, INPUT_PULLUP);//binnen halfvol
  pinMode (sensor4, INPUT_PULLUP);//binnen vol
  pinMode (sensor5, INPUT_PULLUP);//overloop allarm
  pinMode (led1, OUTPUT);//buitenkank leeg
  pinMode (led2, OUTPUT);//binnentank leeg
  pinMode (led3, OUTPUT);//binnentank bhalfvol
  pinMode (led4, OUTPUT);//binnentank vol
  pinMode (led5, OUTPUT);//error
  pinMode (led6, OUTPUT);//pomp

}

void loop() {

  Sensor1 = digitalRead(sensor1); //Buiten leeg
  Sensor2 = digitalRead(sensor2); //Bijna leeg
  Sensor3 = digitalRead(sensor3); //Half
  Sensor4 = digitalRead(sensor4); //Vol
  Sensor5 = digitalRead(sensor5); //Overloop

  // bij defect van een sensor, of overloop, stop. ERROR
   if (Sensor1 == HIGH, Sensor5 == HIGH) {
    digitalWrite(led6, LOW);  //Pomp stopt
    digitalWrite(led5, HIGH); //ERROR led brand
  }
  // als er geen defecten zijn of overloop is, loop dit gedeelte.
  if (Sensor1 == LOW) { // buitentank is leeg
    digitalWrite(led1, HIGH);
    digitalWrite(led6, LOW); //pomp blijft uit
  }
  else {
    digitalWrite(led1, LOW);
  }
  // bij lege tank binnen
  if (Sensor1 == HIGH, Sensor2 == LOW) {
    digitalWrite(led2, HIGH);
    digitalWrite(led6, HIGH);
  }
  else {
    digitalWrite(led2, LOW);
  }
  // als de tank niet geheel leeg is ...
  if (Sensor1, Sensor2 == HIGH) {
    digitalWrite(led2, HIGH);
    digitalWrite(led3, HIGH);
    digitalWrite(led6, HIGH);
  }
  else {
    digitalWrite(led2, LOW);
    digitalWrite(led3, LOW);
  }
  // als de tank halfvol is....
  if (Sensor1, Sensor2, Sensor3 == HIGH) {
    digitalWrite(led3, HIGH);
    digitalWrite(led6, HIGH);
  }
  else {
    digitalWrite(led3, LOW);
  }
  // als de tank vol is
  if (Sensor1, Sensor2, Sensor3, Sensor4 == HIGH) {
    digitalWrite(led4, HIGH);
    digitalWrite(led6, LOW); 
  }
  else {
    digitalWrite(led4, LOW);
  }
}
