# Fritzing sketch Water geven (saved by Fritzing 0.9.6b)
circuit board: 6cm x 9cm
breadboards: 1

parts:
  Sen_A = screw terminal, 3 pins
  Sen_C = screw terminal, 3 pins
  Sen_D = screw terminal, 3 pins
  Sen_E = screw terminal, 3 pins
  Sen_F = screw terminal, 3 pins
  Sen_B = screw terminal, 3 pins
  Sen_G = screw terminal, 3 pins
  Sen_H = screw terminal, 3 pins
  Lijn_4 = Screw terminal - 2 pins [package=THT]
  Lijn_3 = Screw terminal - 2 pins [package=THT]
  Lijn_1 = Screw terminal - 2 pins [package=THT]
  R1 = Resistor [tolerance=±5% power=0.25 resistance=220 package=THT]
  R2 = Resistor [tolerance=±5% power=0.25 resistance=220 package=THT]
  R3 = Resistor [tolerance=±5% power=0.25 resistance=220 package=THT]
  R4 = Resistor [tolerance=±5% power=0.25 resistance=220 package=THT]
  R5 = Resistor [tolerance=±5% power=0.25 resistance=220 package=THT]
  Pomp = LED - 3mm [color="Green (555nm)" current=0.030 package="3 mm [THT]"]
  L3 = LED - 3mm [color="Red (633nm)" current=0.030 package="3 mm [THT]"]
  L2 = LED - 3mm [color="Red (633nm)" current=0.030 package="3 mm [THT]"]
  L1 = LED - 3mm [color="Red (633nm)" current=0.030 package="3 mm [THT]"]
  Arduino_nano = Arduino Nano (Rev3.0)
  Error = Screw terminal - 2 pins [package=THT]
  L5 = LED - 3mm [color="Blue (430nm)" current=0.030 package="3 mm [THT]"]
  R6 = Resistor [tolerance=±5% power=0.25 resistance=220 package=THT]
  Pomp_2 = Screw terminal - 2 pins [package=THT]
  Lijn_2 = Screw terminal - 2 pins [package=THT]
  U6 = Optocoupler [package=THT]
  U7 = Optocoupler [package=THT]
  U8 = Optocoupler [package=THT]
  U9 = Optocoupler [package=THT]
  U10 = Optocoupler [package=THT]
  R7 = Resistor [tolerance=±5% power=0.25 resistance=220 package=THT]
  R8 = Resistor [tolerance=±5% power=0.25 resistance=220 package=THT]
  R9 = Resistor [tolerance=±5% power=0.25 resistance=220 package=THT]
  R10 = Resistor [tolerance=±5% power=0.25 resistance=220 package=THT]
  R11 = Resistor [tolerance=±5% power=0.25 resistance=220 package=THT]
  L4 = LED - 3mm [color="Red (633nm)" current=0.030 package="3 mm [THT]"]

nets:
  N1: Sen_A.pin1, Sen_C.pin1, Sen_D.pin1, Sen_E.pin1, Sen_F.pin1, Sen_B.pin1, Sen_G.pin1, Sen_H.pin1, R1.Pin_0, R2.Pin_0, R3.Pin_0, R4.Pin_0, R5.Pin_0, Arduino_nano.GND, Error.pin2, R6.Pin_0, U6.Pin_2, U7.Pin_2, U8.Pin_2, U9.Pin_2, U10.Pin_2
  N2: Sen_A.pin2, Arduino_nano.A0
  N3: Sen_A.pin3, Sen_C.pin3, Sen_D.pin3, Sen_E.pin3, Sen_F.pin3, Sen_B.pin3, Sen_G.pin3, Sen_H.pin3, Arduino_nano.5V
  N4: Sen_C.pin2, Arduino_nano.A2
  N5: Sen_D.pin2, Arduino_nano.A3
  N6: Sen_E.pin2, Arduino_nano.A4
  N7: Sen_F.pin2, Arduino_nano.A5
  N8: Sen_B.pin2, Arduino_nano.A1
  N9: Sen_G.pin2, Arduino_nano.A6
  N10: Sen_H.pin2, Arduino_nano.A7
  N11: Lijn_4.pin1, U9.Pin_5
  N12: Lijn_4.pin2, U9.Pin_4
  N13: Lijn_3.pin1, U8.Pin_5
  N14: Lijn_3.pin2, U8.Pin_4
  N15: Lijn_1.pin1, U6.Pin_5
  N16: Lijn_1.pin2, U6.Pin_4
  N17: R1.Pin_1, Pomp.cathode
  N18: R2.Pin_1, L4.cathode
  N19: R3.Pin_1, L3.cathode
  N20: R4.Pin_1, L2.cathode
  N21: R5.Pin_1, L1.cathode
  N22: Pomp.anode, Arduino_nano.D6, R11.Pin_0
  N23: L3.anode, Arduino_nano.D4, R9.Pin_0
  N24: L2.anode, Arduino_nano.D3, R8.Pin_0
  N25: L1.anode, Arduino_nano.D2, R7.Pin_0
  N26: Arduino_nano.D5, R10.Pin_0, L4.anode
  N27: Arduino_nano.D7, Error.pin1, L5.anode
  N28: L5.cathode, R6.Pin_1
  N29: Pomp_2.pin1, U10.Pin_5
  N30: Pomp_2.pin2, U10.Pin_4
  N31: Lijn_2.pin1, U7.Pin_5
  N32: Lijn_2.pin2, U7.Pin_4
  N33: U6.Pin_1, R7.Pin_1
  N34: U7.Pin_1, R8.Pin_1
  N35: U8.Pin_1, R9.Pin_1
  N36: U9.Pin_1, R10.Pin_1
  N37: U10.Pin_1, R11.Pin_1

// code stored in the sketch: Water_geven.ino
#define SenA A0
#define SenB A1
#define SenC A2
#define SenD A3
#define SenE A4
#define SenF A5
#define SenG A6
#define SenH A7
#define Lijn1 2
#define Lijn2 3
#define Lijn3 4
#define Lijn4 5
#define Pomp  6
#define Error 7

const int AirValueA = 610;   // This is the value of your sensor when you place it in the open air
const int WaterValueA = 260;  // This is the value when you place your sensor in a glass of water
int valueA = 0;
int percentA = 0;

const int AirValueB = 605;   // This is the value of your sensor when you place it in the open air
const int WaterValueB = 270;  // This is the value when you place your sensor in a glass of water
int valueB = 0;
int percentB = 0;

const int AirValueC = 611;   // This is the value of your sensor when you place it in the open air
const int WaterValueC = 259;  // This is the value when you place your sensor in a glass of water
int valueC = 0;
int percentC = 0;

const int AirValueD = 612;   // This is the value of your sensor when you place it in the open air
const int WaterValueD = 262;  // This is the value when you place your sensor in a glass of water
int valueD = 0;
int percentD = 0;

const int AirValueE = 615;   // This is the value of your sensor when you place it in the open air
const int WaterValueE = 270;  // This is the value when you place your sensor in a glass of water
int valueE = 0;
int percentE = 0;

const int AirValueF = 613;   // This is the value of your sensor when you place it in the open air
const int WaterValueF = 266;  // This is the value when you place your sensor in a glass of water
int valueF = 0;
int percentF = 0;

const int AirValueG = 613;   // This is the value of your sensor when you place it in the open air
const int WaterValueG = 266;  // This is the value when you place your sensor in a glass of water
int valueG = 0;
int percentG = 0;

const int AirValueH = 613;   // This is the value of your sensor when you place it in the open air
const int WaterValueH = 266;  // This is the value when you place your sensor in a glass of water
int valueH = 0;
int percentH = 0;

int gemAB = 0;
int gemCD = 0;
int gemEF = 0;
int gemGH = 0;
int ERROR = 0

void setup() {

  pinMode(SenA, INPUT);
  pinMode(SenB, INPUT);
  pinMode(SenC, INPUT);
  pinMode(SenD, INPUT);
  pinMode(SenE, INPUT);
  pinMode(SenF, INPUT);
  pinMode(SenG, INPUT);
  pinMode(SenH, INPUT);
  pinMode(Lijn1, OUTPUT);
  pinMode(Lijn2, OUTPUT);
  pinMode(Lijn3, OUTPUT);
  pinMode(Lijn4, OUTPUT);
  pinMode(Pomp, OUTPUT);
  pinMode(Error, INPUT);
}

void loop() {

  if (ERROR == HIGH){
     digitalWrite(Pomp, LOW);
}
else{

  valueA = analogRead(A0);
  valueB = analogRead(A1);
  valueC = analogRead(A2);
  valueD = analogRead(A3);
  valueE = analogRead(A4);
  valueF = analogRead(A5);
  valueG = analogRead(A6);
  valueH = analogRead(A7);

  percentA = map(valueA, AirValueA, WaterValueA, 0, 100);
  percentB = map(valueB, AirValueB, WaterValueB, 0, 100);
  percentC = map(valueC, AirValueC, WaterValueC, 0, 100);
  percentD = map(valueD, AirValueD, WaterValueD, 0, 100);
  percentE = map(valueE, AirValueE, WaterValueE, 0, 100);
  percentF = map(valueF, AirValueF, WaterValueF, 0, 100);
  percentG = map(valueG, AirValueG, WaterValueG, 0, 100);
  percentF = map(valueH, AirValueH, WaterValueH, 0, 100);

  gemAB = (percentA + percentB) / 2;
  gemCD = (percentC + percentD) / 2;
  gemEF = (percentE + percentF) / 2;
  gemGH = (percentG + percentH) / 2;

  if (gemAB <= 20) {
    digitalWrite(Pomp, HIGH);
    digitalWrite(Lijn1, HIGH);
  }
  if (gemAB >= 80) {
    digitalWrite(Pomp, LOW);
    digitalWrite(Lijn1, LOW);
  }
  if (gemCD <= 20) {
    digitalWrite(Pomp, HIGH);
    digitalWrite(Lijn2, HIGH);
  }
  if (gemCD >= 80) {
    digitalWrite(Pomp, LOW);
    digitalWrite(Lijn2, LOW);
  }
  if (gemEF <= 20) {
    digitalWrite(Pomp, HIGH);
    digitalWrite(Lijn3, HIGH);
  }
  if (gemEF >= 80) {
    digitalWrite(Pomp, LOW);
    digitalWrite(Lijn3, LOW);
  }
if (gemGH <= 20) {
    digitalWrite(Pomp, HIGH);
    digitalWrite(Lijn4, HIGH);
  }
  if (gemGH >= 80) {
    digitalWrite(Pomp, LOW);
    digitalWrite(Lijn4, LOW);
  }
}
