# Fritzing sketch Zonblok serre2 (saved by Fritzing 0.9.6b)
circuit board: 6cm x 9cm
breadboards: 1

parts:
  Motor_raam = screw terminal, 4 pins
  Motor_Scherm = screw terminal, 4 pins
  Scherm_Uit = screw terminal, 3 pins
  Scherm_in = screw terminal, 3 pins
  Raam_Toe = screw terminal, 3 pins
  LED_Scherm = DUO LED RG [package="5 mm [THT]"]
  Arduino_nano = Arduino Nano (Rev3.0)
  DHT = screw terminal, 3 pins
  Raam_Open = screw terminal, 3 pins
  Pololu_A1 = Pololu A4988 [package=SO16]
  Pololu_A2 = Pololu A4988 [package=SO16]
  12_V = Screw terminal - 2 pins [package=THT]
  LED_Rel = LED - 3mm [color="Green (555nm)" current=0.030 package="3 mm [THT]"]
  LED_Raam = DUO LED RG [package="5 mm [THT]"]
  Relais = screw terminal, 3 pins

nets:
  N1: Motor_raam.pin1, Pololu_A2.2B
  N2: Motor_raam.pin2, Pololu_A2.2A
  N3: Motor_raam.pin3, Pololu_A2.1A
  N4: Motor_raam.pin4, Pololu_A2.1B
  N5: Motor_Scherm.pin1, Pololu_A1.2B
  N6: Motor_Scherm.pin2, Pololu_A1.2A
  N7: Motor_Scherm.pin3, Pololu_A1.1A
  N8: Motor_Scherm.pin4, Pololu_A1.1B
  VDD: Scherm_Uit.pin1, Scherm_in.pin1, Raam_Toe.pin1, Arduino_nano.5V, DHT.pin1, Raam_Open.pin1, Pololu_A1.VDD, Pololu_A2.VDD
  N9: Scherm_Uit.pin2, Arduino_nano.D11/MOSI, LED_Raam.red_anode
  N10: Scherm_Uit.pin3, Scherm_in.pin3, Raam_Toe.pin3, LED_Scherm.common_cathode, Arduino_nano.GND, DHT.pin3, Raam_Open.pin3, Pololu_A1.GND#8, Pololu_A2.GND#8, 12_V.pin1, LED_Rel.cathode, LED_Raam.common_cathode, Relais.pin1
  N11: Scherm_in.pin2, Arduino_nano.D10, LED_Raam.green_anode
  N12: Raam_Toe.pin2, LED_Scherm.green_anode, Arduino_nano.D9
  N13: LED_Scherm.red_anode, Arduino_nano.D8, Raam_Open.pin2
  N14: Arduino_nano.D2, DHT.pin2
  N15: Arduino_nano.D3, Pololu_A2.STEP
  N16: Arduino_nano.D4, Pololu_A2.DIR
  N17: Arduino_nano.D5, Pololu_A1.STEP
  N18: Arduino_nano.D6, Pololu_A1.DIR
  N19: Arduino_nano.D7, LED_Rel.anode, Relais.pin2
  N20: Pololu_A1.RESET, Pololu_A1.SLEEP
  N21: Pololu_A1.GND#14, Pololu_A2.GND#14
  N22: Pololu_A1.VMOT, Pololu_A2.VMOT, 12_V.pin2, Relais.pin3
  N23: Pololu_A2.RESET, Pololu_A2.SLEEP

// code stored in the sketch: Raam_Serre.ino
#include "DHT.h"

#define DHTPIN 2
#define StepRaam 3
#define DirRaam 4
#define StepScherm 5
#define DirScherm 6
#define Rel 7
#define StopOpen 8
#define StopToe 9
#define SchermIn 10
#define SchermUit 11

#define DHTTYPE DHT22
DHT dht(DHTPIN, DHTTYPE);

void setup() {

  dht.begin();
  pinMode(StepRaam, OUTPUT);
  pinMode(DirRaam, OUTPUT);
  pinMode(StepScherm, OUTPUT);
  pinMode(DirScherm, OUTPUT);
  pinMode(Rel, OUTPUT);
  pinMode(StopOpen, INPUT);
  pinMode(StopToe, INPUT);
  pinMode(SchermIn, INPUT);
  pinMode(SchermUit, INPUT);
}

void loop() {
  if (dht.readTemperature() == 18) {
    digitalWrite(Rel, HIGH);
    RaamOpen();
  }
  if (dht.readTemperature() == 34) {
    digitalWrite(Rel, HIGH);
    RaamToe();
  }
  if (dht.readTemperature() == 35) {
    digitalWrite(Rel, HIGH);
    SchermDicht();
  }
  if (dht.readTemperature() == 20) {
    digitalWrite(Rel, HIGH);
    SchermOpen();
  }
}

// code stored in the sketch: Untitled2.ino
/*Deze schets is een van de 3 delen die een serre bewaken en besturen.
  Een Nano zorgt voor de temperatuur in de serre tijdens de zomer, te
  heet, raam open, zo nodig een verduisterscherm, bestaande uit een witte
  doek die aan de buitenkant uitgerold wordt om de zon in zijn kracht te 
  weren. Er is in gedachten een systeem in wording om eventueel een
  geforseerde luchtsyrculatie te verkoeling uit te bouwen me een vernevel 
  instalatie die een mist van water voorziet ter afkoeling.
  Er komt ook nog een uitbrijding bij voor verwarming om in de winter 
  de koning uit de serre te houden, die kan evenveel, of nog meer schade 
  toebrengen aan de planten als teveel hitte.
  .......
*/

#include "DHT.h"

#define DHTPIN      2
#define StepRaam    3
#define DirRaam     4
#define StepScherm  5
#define DirScherm   6
#define Rel         7
#define Raam1       8
#define Raam2       9
#define Scherm1     10
#define Scherm2     11

#define DHTTYPE DHT22
DHT dht(DHTPIN, DHTTYPE);

void setup() {
  dht.begin();
  /*De stepmotoren zijn niet zeker te blijven, 
  kunnen vervangen worden door gewone motoren 
  */
  pinMode(StepRaam, OUTPUT);
  pinMode(DirRaam, OUTPUT);
  pinMode(StepScherm, OUTPUT);
  pinMode(DirScherm, OUTPUT);
  pinMode(Rel, OUTPUT);//Stroomvoorziening motoren aan/uit
  pinMode(Raam1, INPUT);//Stop als het raam geheel open is
  pinMode(Raam2, INPUT);//Stop als het raam geheel dicht is
  pinMode(Scherm1, INPUT);//Stop als het scherm uitgerold is
  pinMode(Scherm2, INPUT);//Stop als het scherm opgerold is
}

void loop() {
  //Bij 18?C mag het raam open als het scherm opgerold is aangegeven.
  if (dht.readTemperature() == 18 & Scherm2 == HIGH) {
    digitalWrite(Rel, HIGH);
    RaamOpen();
  }
  //Bij een tem van 30?C, raam dicht en scherm uitrollen.
  if (dht.readTemperature() == 30) {
    digitalWrite(Rel, HIGH);
    RaamDicht();
  }
  if (dht.readTemperature() == 30 & Raam2 == HIGH) {
    digitalWrite(Rel, HIGH);
    SchermUitrollen();
  }
  //Als de temp gezakt is tot 28?C, scherm oprollen en raam open.
  if (dht. readTemperature() == 28) {
    digitalWrite(Rel, HIGH);
    SchermOprollen();
  }
}

void RaamOpen() {

  digitalWrite(DirRaam, HIGH);
  digitalWrite(StepRaam, HIGH);
  delayMicroseconds(200);
  digitalWrite(StepRaam, LOW);
  delayMicroseconds(200);
  if (digitalRead(Raam1) == HIGH) {
    digitalWrite(Rel, LOW);
  }
}

void RaamDicht() {
  digitalWrite(DirRaam, LOW);
  digitalWrite(StepRaam ,HIGH);
  delayMicroseconds(200);
  digitalWrite(StepRaam, LOW);
  delayMicroseconds(200);
  if (digitalRead(Raam2) == HIGH) {
    digitalWrite(Rel, LOW);
  }
}

void SchermOprollen(){
  digitalWrite(DirScherm, LOW);
  digitalWrite(StepScherm, HIGH);
  delayMicroseconds(200);
  digitalWrite(StepScherm, LOW);
  delayMicroseconds(200);
  if (digitalRead(Scherm1) == HIGH) {
    digitalWrite(Rel, LOW);
  }
}

void SchermUitrollen(){
  digitalWrite(DirScherm, HIGH);
  digitalWrite(StepScherm, LOW);
  delayMicroseconds(200);
  digitalWrite(StepScherm, HIGH);
  delayMicroseconds(200);
  if(digitalRead(Scherm2) == HIGH){
    digitalWrite(Rel, LOW);
  }
}
